# Fritzing sketch Regolazione della velocità del motore con PWM (saved by Fritzing 0.9.3b)
breadboards: 1

parts:
  Componente1 = Arduino Uno (Rev3)
  Q1 = NPN-Transistor [package="TO92 [THT]"]
  D1 = Rectifier Diode [part_number=1N4001 package="300 mil [THT]"]
  M1 = DC Motor
  R2 = Resistor [tolerance=±5% resistance=220 package=THT]
  R3 = Rotary Potentiometer (Small) [maximum_resistance=100kΩ package=THT]

nets:
  N1: Componente1.A0, R3.wiper
  N2: Componente1.D5_PWM, R2.Pin_1
  N3: Componente1.5V, D1.anode, M1.pin_1
  N4: Componente1.GND, Q1.C, R3.leg1
  N5: Q1.B, R2.Pin_0
  N6: D1.cathode, M1.pin_2
